// Logisim project pratical.3 half and full adder.circ as structural Verilog: 1 circuit, main circuit main
module main (
  input  A,
  input  B,
  input  A_2,
  input  B_2,
  input  C,
  output sum,
  output carry,
  output out_8,
  output carry_2
);

  wire and_2_out, and_3_out, xor_1_out;

  xor xor_1 (xor_1_out, A_2, B_2);
  xor xor_2 (sum, A, B);
  and and_1 (carry, B, A);
  xor xor_3 (out_8, xor_1_out, C);
  and and_2 (and_2_out, C, xor_1_out);
  and and_3 (and_3_out, B_2, A_2);
  or or_1 (carry_2, and_2_out, and_3_out);

  // Notes on the sheet:
  //   sum
endmodule
